// Logisim project Pattern_Detector.circ as structural Verilog: 1 circuit, main circuit main
module main (
  input  in_1,
  input  in_2,
  input  in_3,
  input  in_4,
  input  in_5,
  input  in_6,
  input  in_7,
  input  in_8,
  input  in_9,
  input  in_10,
  input  in_11,
  input  in_12,
  input  in_13,
  input  in_14,
  input  in_15,
  input  in_16,
  input  in_17,
  input  in_18,
  input  in_19,
  input  in_20,
  input  PINS,
  input  in_22,
  input  in_23,
  input  in_24,
  input  in_25,
  input  in_26,
  input  in_27,
  input  in_28,
  input  in_29,
  input  in_30,
  input  in_31,
  input  in_32
);

  wire and_1_out, and_2_out, and_3_out, and_4_out, and_5_out, and_6_out, and_7_out, and_8_out, and_9_out,
       and_10_out, and_11_out, and_12_out, and_13_out, and_14_out, and_15_out, and_16_out, and_17_out,
       not_1_out, xnor_1_out, xnor_2_out, xnor_3_out, xnor_4_out, xnor_5_out, xnor_6_out, xnor_7_out,
       xnor_8_out, xnor_9_out, xnor_10_out, xnor_11_out, xnor_12_out, xnor_13_out, xnor_14_out, xnor_15_out,
       xnor_16_out;

  LED led_1 (.in(in_1));
  LED led_2 (.in(in_2));
  LED led_3 (.in(in_9));
  LED led_4 (.in(in_10));
  LED led_5 (.in(in_17));
  LED led_6 (.in(in_18));
  LED led_7 (.in(PINS));
  LED led_8 (.in(in_22));
  LED led_9 (.in(in_3));
  LED led_10 (.in(in_11));
  LED led_11 (.in(in_19));
  LED led_12 (.in(in_23));
  LED led_13 (.in(in_4));
  LED led_14 (.in(in_12));
  LED led_15 (.in(in_20));
  LED led_16 (.in(in_24));
  and and_1 (and_1_out, in_1, in_5);
  and and_2 (and_2_out, in_9, in_13);
  and and_3 (and_3_out, in_17, in_25);
  and and_4 (and_4_out, PINS, in_29);
  and and_5 (and_5_out, in_2, in_6);
  and and_6 (and_6_out, in_10, in_14);
  and and_7 (and_7_out, in_18, in_26);
  and and_8 (and_8_out, in_22, in_30);
  and and_9 (and_9_out, in_3, in_7);
  and and_10 (and_10_out, in_11, in_15);
  and and_11 (and_11_out, in_19, in_27);
  and and_12 (and_12_out, in_23, in_31);
  and and_13 (and_13_out, in_4, in_8);
  and and_14 (and_14_out, in_12, in_16);
  and and_15 (and_15_out, in_20, in_28);
  and and_16 (and_16_out, in_24, in_32);
  LED led_17 (.in(and_1_out));
  LED led_18 (.in(and_5_out));
  LED led_19 (.in(and_2_out));
  LED led_20 (.in(and_6_out));
  LED led_21 (.in(and_3_out));
  LED led_22 (.in(and_7_out));
  LED led_23 (.in(and_4_out));
  LED led_24 (.in(and_8_out));
  LED led_25 (.in(and_9_out));
  LED led_26 (.in(and_10_out));
  LED led_27 (.in(and_11_out));
  LED led_28 (.in(and_12_out));
  LED led_29 (.in(and_13_out));
  LED led_30 (.in(and_14_out));
  LED led_31 (.in(and_15_out));
  LED led_32 (.in(and_16_out));
  xnor xnor_1 (xnor_1_out, and_1_out, in_5);
  xnor xnor_2 (xnor_2_out, and_2_out, in_13);
  xnor xnor_3 (xnor_3_out, in_25, and_3_out);
  xnor xnor_4 (xnor_4_out, in_29, and_4_out);
  xnor xnor_5 (xnor_5_out, and_5_out, in_6);
  xnor xnor_6 (xnor_6_out, and_6_out, in_14);
  xnor xnor_7 (xnor_7_out, in_26, and_7_out);
  xnor xnor_8 (xnor_8_out, in_30, and_8_out);
  xnor xnor_9 (xnor_9_out, and_9_out, in_7);
  xnor xnor_10 (xnor_10_out, and_10_out, in_15);
  xnor xnor_11 (xnor_11_out, in_27, and_11_out);
  xnor xnor_12 (xnor_12_out, in_31, and_12_out);
  xnor xnor_13 (xnor_13_out, and_13_out, in_8);
  xnor xnor_14 (xnor_14_out, and_14_out, in_16);
  xnor xnor_15 (xnor_15_out, in_28, and_15_out);
  xnor xnor_16 (xnor_16_out, in_32, and_16_out);
  and and_17 (and_17_out, xnor_10_out, xnor_9_out, xnor_6_out, xnor_5_out, xnor_1_out, xnor_2_out, xnor_13_out, xnor_14_out, xnor_15_out, xnor_16_out, xnor_3_out, xnor_4_out, xnor_7_out, xnor_8_out, xnor_11_out, xnor_12_out);
  LED led_33 (.in(and_17_out));
  not not_1 (not_1_out, and_17_out);
  LED led_34 (.in(not_1_out));

  // Notes on the sheet:
  //   INPUT
  //   WEIGHT
  //   OUTPUT
  //   DECISION-MAKER
  //   RECOGNIZED
  //   NOT RECOGNIZED
endmodule
