// Logisim project Pattern_Detector_Adaptive_Learning_MIDS.circ as structural Verilog: 16 circuits, main circuit main
module main (
  input  in_1,
  input  in_2,
  input  in_3,
  input  in_4,
  input  in_5,
  input  in_6,
  input  in_7,
  input  in_8,
  input  in_9,
  input  in_10,
  input  in_11,
  input  in_12,
  input  in_13,
  input  in_14,
  input  in_15,
  input  in_16,
  input  in_17,
  input  in_18,
  input  in_19,
  input  in_20,
  input  in_21,
  input  in_22,
  input  in_23,
  input  in_24,
  input  in_25,
  input  in_26,
  input  in_27,
  input  in_28,
  input  in_29,
  input  in_30,
  input  in_31,
  input  in_32,
  input  in_33,
  input  in_34,
  input  in_35,
  input  in_36,
  input  in_37,
  input  in_38,
  input  in_39,
  input  in_40,
  input  in_41,
  input  in_42,
  input  in_43,
  input  in_44,
  input  in_45,
  input  in_46,
  input  in_47,
  input  in_48
);

  wire button_1_out, control_loop_1_ad_seq, control_loop_1_to1, control_loop_1_to2, control_loop_1_to4,
       control_loop_1_to8, or_1_out, rgbled_1_p1, super_system_1_ad_seq_success, super_system_1_haz_nul,
       super_system_1_mpa, super_system_1_mpb, super_system_1_mpc, super_system_1_mpd, super_system_1_mpe,
       super_system_1_mpf, super_system_1_mpg, super_system_1_mta, super_system_1_mtb, super_system_1_mtc,
       super_system_1_mtd, super_system_1_mte, super_system_1_mtf, super_system_1_mtg, super_system_1_pa,
       super_system_1_pb, super_system_1_pc, super_system_1_pd, super_system_1_pe, super_system_1_pf,
       super_system_1_pg, super_system_1_rearm_seq, super_system_1_recognition, super_system_1_ta,
       super_system_1_tb, super_system_1_tc, super_system_1_td, super_system_1_te, super_system_1_tf,
       super_system_1_tg, super_system_1_tim_haz_det, xnor_1_out, xnor_2_out, xnor_3_out, xnor_4_out,
       xnor_5_out, xnor_6_out, xnor_7_out, xnor_8_out, xnor_9_out, xnor_10_out, xnor_11_out, xnor_12_out,
       xnor_13_out, xnor_14_out, xnor_15_out, xnor_16_out;

  LED led_1 (.in(in_14));
  LED led_2 (.in(in_22));
  LED led_3 (.in(in_30));
  LED led_4 (.in(in_38));
  LED led_5 (.in(in_15));
  LED led_6 (.in(in_16));
  LED led_7 (.in(in_23));
  LED led_8 (.in(in_24));
  LED led_9 (.in(in_31));
  LED led_10 (.in(in_32));
  LED led_11 (.in(in_39));
  LED led_12 (.in(in_40));
  LED led_13 (.in(in_17));
  LED led_14 (.in(in_25));
  LED led_15 (.in(in_33));
  LED led_16 (.in(in_41));
  LED led_17 (.in(in_18));
  LED led_18 (.in(in_26));
  LED led_19 (.in(in_34));
  LED led_20 (.in(in_42));
  LED led_21 (.in(in_19));
  LED led_22 (.in(in_27));
  LED led_23 (.in(in_35));
  LED led_24 (.in(in_43));
  LED led_25 (.in(in_20));
  LED led_26 (.in(in_21));
  LED led_27 (.in(in_28));
  LED led_28 (.in(in_29));
  LED led_29 (.in(in_36));
  LED led_30 (.in(in_37));
  LED led_31 (.in(in_44));
  LED led_32 (.in(in_45));
  xnor xnor_1 (xnor_1_out, in_18, in_14);
  xnor xnor_2 (xnor_2_out, in_26, in_22);
  xnor xnor_3 (xnor_3_out, in_30, in_34);
  xnor xnor_4 (xnor_4_out, in_38, in_42);
  xnor xnor_5 (xnor_5_out, in_19, in_15);
  xnor xnor_6 (xnor_6_out, in_27, in_23);
  xnor xnor_7 (xnor_7_out, in_31, in_35);
  xnor xnor_8 (xnor_8_out, in_39, in_43);
  xnor xnor_9 (xnor_9_out, in_20, in_16);
  xnor xnor_10 (xnor_10_out, in_28, in_24);
  xnor xnor_11 (xnor_11_out, in_32, in_36);
  xnor xnor_12 (xnor_12_out, in_40, in_44);
  Button button_1 (.out(button_1_out));
  xnor xnor_13 (xnor_13_out, in_21, in_17);
  xnor xnor_14 (xnor_14_out, in_29, in_25);
  xnor xnor_15 (xnor_15_out, in_33, in_37);
  xnor xnor_16 (xnor_16_out, in_41, in_45);
  // RGBLED rgbled_1: pin names not known; wires that end beside it: rgbled_1_p1
  control_loop control_loop_1 (
    .MEM_RST(in_1), .MEM_P_EN(in_2), .D1(in_3), .D2(in_4), .D4(in_5), .D8(in_6), .ERROR_IN(button_1_out),
    .E0W1(in_7), .M_LRST(in_8), .T8(in_9), .T4(in_10), .T2(in_11), .T1(in_12), .M_TL(in_13),
    .rearm(super_system_1_rearm_seq), .CLK(rgbled_1_p1), .TO8(control_loop_1_to8), .TO4(control_loop_1_to4),
    .TO2(control_loop_1_to2), .TO1(control_loop_1_to1), .ad_seq(control_loop_1_ad_seq));  // open: A1V, A2V, A4V, A8V
  // RGBLED rgbled_2: pin names not known
  // RGBLED rgbled_3: pin names not known
  // RGBLED rgbled_4: pin names not known
  // RGBLED rgbled_5: pin names not known
  or or_1 (or_1_out, in_46, super_system_1_rearm_seq);
  Super_System super_system_1 (
    .T8(control_loop_1_to8), .T4(control_loop_1_to4), .T2(control_loop_1_to2), .T1(control_loop_1_to1),
    .I1(xnor_10_out), .I2(xnor_9_out), .I3(xnor_6_out), .I4(xnor_5_out), .I5(xnor_1_out), .I6(xnor_2_out),
    .I7(xnor_13_out), .I8(xnor_14_out), .I9(xnor_15_out), .I10(xnor_16_out), .I11(xnor_3_out),
    .I12(xnor_4_out), .I13(xnor_7_out), .I14(xnor_8_out), .I15(xnor_11_out), .I16(xnor_12_out),
    .cnvd_rst(or_1_out), .ad_seq(control_loop_1_ad_seq), .clr_sf(in_47), .rst_haz_track(in_48),
    .MPB(super_system_1_mpb), .MPA(super_system_1_mpa), .MPG(super_system_1_mpg), .MPF(super_system_1_mpf),
    .MPE(super_system_1_mpe), .MPD(super_system_1_mpd), .MPC(super_system_1_mpc), .PB(super_system_1_pb),
    .PA(super_system_1_pa), .PG(super_system_1_pg), .PF(super_system_1_pf), .PE(super_system_1_pe),
    .PD(super_system_1_pd), .PC(super_system_1_pc), .RECOGNITION(super_system_1_recognition),
    .ad_seq_success(super_system_1_ad_seq_success), .MTB(super_system_1_mtb), .MTA(super_system_1_mta),
    .MTG(super_system_1_mtg), .MTF(super_system_1_mtf), .MTE(super_system_1_mte), .MTD(super_system_1_mtd),
    .MTC(super_system_1_mtc), .TB(super_system_1_tb), .TA(super_system_1_ta), .TG(super_system_1_tg),
    .TF(super_system_1_tf), .TE(super_system_1_te), .TD(super_system_1_td), .TC(super_system_1_tc),
    .rearm_seq(super_system_1_rearm_seq), .tim_haz_det(super_system_1_tim_haz_det),
    .Haz_nul(super_system_1_haz_nul));
  _7_Segment_Display u_7_segment_display_1 (
    .g(super_system_1_mpg), .f(super_system_1_mpf), .a(super_system_1_mpa), .b(super_system_1_mpb),
    .e(super_system_1_mpe), .d(super_system_1_mpd), .c(super_system_1_mpc));  // open: dp
  _7_Segment_Display u_7_segment_display_2 (
    .g(super_system_1_pg), .f(super_system_1_pf), .a(super_system_1_pa), .b(super_system_1_pb),
    .e(super_system_1_pe), .d(super_system_1_pd), .c(super_system_1_pc));  // open: dp
  LED led_33 (.in(super_system_1_recognition));
  // RGBLED rgbled_6: pin names not known; wires that end beside it: super_system_1_ad_seq_success
  _7_Segment_Display u_7_segment_display_3 (
    .g(super_system_1_mtg), .f(super_system_1_mtf), .a(super_system_1_mta), .b(super_system_1_mtb),
    .e(super_system_1_mte), .d(super_system_1_mtd), .c(super_system_1_mtc));  // open: dp
  _7_Segment_Display u_7_segment_display_4 (
    .g(super_system_1_tg), .f(super_system_1_tf), .a(super_system_1_ta), .b(super_system_1_tb),
    .e(super_system_1_te), .d(super_system_1_td), .c(super_system_1_tc));  // open: dp
  LED led_34 (.in(super_system_1_tim_haz_det));
  // RGBLED rgbled_7: pin names not known; wires that end beside it: super_system_1_haz_nul

  // Notes on the sheet:
  //   INPUT
  //   ADAPTIVE LEARNING SYSTEM
  //   Autonomously Alters its own Decision Boundary based on Error Input
  //   REFERENCE
  //   X-NOR EQUIVALENCE  GRID
  //   Control and Setup Pins
  //   Error_IN
  //   ADAPTIVE
  //   THRESHOLD
  //   LOOP
  //   Clear Convergence Detectors
  //   Clear Success Flag
  //   Clear Error Flag
  //   CYBERNETIC 
  //   CONTROL
  //   Threshold 
  //   Pointer
  //   MATCHED
  //   PIXELS
  //   RECOGNITION
  //   CORRECTION
  //   THRESHOLD
  //   Hazard Detected
  //   Hazard Nullified
endmodule

module Half_adder (
  input  A,
  input  B,
  output SUM,
  output CARRY
);

  wire and_1_out, and_2_out, not_1_out, not_2_out;

  not not_1 (not_1_out, A);
  not not_2 (not_2_out, B);
  and and_1 (and_1_out, not_1_out, B);
  and and_2 (and_2_out, A, not_2_out);
  and and_3 (CARRY, A, B);
  or or_1 (SUM, and_1_out, and_2_out);

  // Notes on the sheet:
  //   HALF ADDER
endmodule

module POP_Counter (
  input  I1,
  input  I2,
  input  I3,
  input  I4,
  input  I5,
  input  I6,
  input  I7,
  input  I8,
  input  I9,
  input  I10,
  input  I11,
  input  I12,
  input  I13,
  input  I14,
  input  I15,
  input  I16,
  output W16,
  output W8,
  output W4,
  output W2,
  output W1
);

  wire half_adder_1_carry, half_adder_1_sum, half_adder_2_carry, half_adder_2_sum, half_adder_3_carry,
       half_adder_3_sum, half_adder_4_carry, half_adder_4_sum, half_adder_5_carry, half_adder_5_sum,
       half_adder_6_carry, half_adder_6_sum, half_adder_7_carry, half_adder_7_sum, half_adder_8_carry,
       half_adder_8_sum, half_adder_9_carry, half_adder_9_sum, half_adder_10_carry, half_adder_10_sum,
       half_adder_11_carry, half_adder_11_sum, half_adder_12_carry, half_adder_12_sum, half_adder_13_carry,
       half_adder_13_sum, half_adder_14_carry, half_adder_14_sum, half_adder_15_carry, half_adder_15_sum,
       half_adder_16_carry, half_adder_16_sum, half_adder_17_carry, half_adder_17_sum, half_adder_18_carry,
       half_adder_18_sum, half_adder_19_carry, half_adder_19_sum, half_adder_20_carry, half_adder_20_sum,
       half_adder_21_carry, half_adder_21_sum, half_adder_22_carry, half_adder_22_sum, half_adder_23_carry,
       half_adder_23_sum, half_adder_24_carry, half_adder_24_sum, half_adder_25_carry, half_adder_25_sum,
       half_adder_26_carry, half_adder_26_sum, half_adder_27_carry, half_adder_28_carry, half_adder_28_sum,
       half_adder_29_carry, half_adder_29_sum, half_adder_30_carry, half_adder_30_sum, half_adder_31_carry,
       half_adder_31_sum, half_adder_32_carry, half_adder_32_sum, half_adder_33_carry, half_adder_33_sum,
       half_adder_34_carry, half_adder_34_sum, half_adder_35_carry, half_adder_35_sum, half_adder_36_carry,
       half_adder_36_sum, half_adder_37_carry, half_adder_37_sum, half_adder_38_sum, half_adder_39_carry,
       half_adder_39_sum, half_adder_40_carry, half_adder_40_sum, half_adder_41_carry, half_adder_41_sum,
       half_adder_42_carry, half_adder_42_sum, half_adder_43_carry, half_adder_43_sum, half_adder_44_carry,
       half_adder_44_sum, half_adder_45_carry, half_adder_46_carry, half_adder_46_sum, half_adder_47_sum,
       half_adder_48_sum, half_adder_49_carry, half_adder_49_sum, half_adder_50_carry, half_adder_50_sum,
       half_adder_51_sum, half_adder_52_sum, half_adder_53_carry, half_adder_53_sum, half_adder_54_carry,
       half_adder_55_sum, half_adder_56_carry, half_adder_56_sum, half_adder_57_sum, half_adder_58_carry,
       half_adder_58_sum, half_adder_59_sum, half_adder_60_carry, half_adder_60_sum, half_adder_61_sum,
       half_adder_62_carry, half_adder_63_sum;

  Half_adder half_adder_1 (.A(I1), .B(I2), .SUM(half_adder_1_sum), .CARRY(half_adder_1_carry));
  Half_adder half_adder_2 (.A(I3), .B(I4), .SUM(half_adder_2_sum), .CARRY(half_adder_2_carry));
  Half_adder half_adder_3 (.A(I5), .B(I6), .SUM(half_adder_3_sum), .CARRY(half_adder_3_carry));
  Half_adder half_adder_4 (.A(I7), .B(I8), .SUM(half_adder_4_sum), .CARRY(half_adder_4_carry));
  Half_adder half_adder_5 (.A(I9), .B(I10), .SUM(half_adder_5_sum), .CARRY(half_adder_5_carry));
  Half_adder half_adder_6 (.A(I11), .B(I12), .SUM(half_adder_6_sum), .CARRY(half_adder_6_carry));
  Half_adder half_adder_7 (.A(I13), .B(I14), .SUM(half_adder_7_sum), .CARRY(half_adder_7_carry));
  Half_adder half_adder_8 (.A(I15), .B(I16), .SUM(half_adder_8_sum), .CARRY(half_adder_8_carry));
  Half_adder half_adder_9 (
    .A(half_adder_1_sum), .B(half_adder_2_sum), .SUM(half_adder_9_sum), .CARRY(half_adder_9_carry));
  Half_adder half_adder_10 (
    .A(half_adder_1_carry), .B(half_adder_2_carry), .SUM(half_adder_10_sum), .CARRY(half_adder_10_carry));
  Half_adder half_adder_11 (
    .A(half_adder_3_sum), .B(half_adder_4_sum), .SUM(half_adder_11_sum), .CARRY(half_adder_11_carry));
  Half_adder half_adder_12 (
    .A(half_adder_3_carry), .B(half_adder_4_carry), .SUM(half_adder_12_sum), .CARRY(half_adder_12_carry));
  Half_adder half_adder_13 (
    .A(half_adder_5_sum), .B(half_adder_6_sum), .SUM(half_adder_13_sum), .CARRY(half_adder_13_carry));
  Half_adder half_adder_14 (
    .A(half_adder_5_carry), .B(half_adder_6_carry), .SUM(half_adder_14_sum), .CARRY(half_adder_14_carry));
  Half_adder half_adder_15 (
    .A(half_adder_7_sum), .B(half_adder_8_sum), .SUM(half_adder_15_sum), .CARRY(half_adder_15_carry));
  Half_adder half_adder_16 (
    .A(half_adder_7_carry), .B(half_adder_8_carry), .SUM(half_adder_16_sum), .CARRY(half_adder_16_carry));
  Half_adder half_adder_17 (
    .A(half_adder_10_carry), .B(half_adder_12_carry), .SUM(half_adder_17_sum), .CARRY(half_adder_17_carry));
  Half_adder half_adder_18 (
    .A(half_adder_9_carry), .B(half_adder_11_carry), .SUM(half_adder_18_sum), .CARRY(half_adder_18_carry));
  Half_adder half_adder_19 (
    .A(half_adder_9_sum), .B(half_adder_11_sum), .SUM(half_adder_19_sum), .CARRY(half_adder_19_carry));
  Half_adder half_adder_20 (
    .A(half_adder_10_sum), .B(half_adder_12_sum), .SUM(half_adder_20_sum), .CARRY(half_adder_20_carry));
  Half_adder half_adder_21 (
    .A(half_adder_14_sum), .B(half_adder_16_sum), .SUM(half_adder_21_sum), .CARRY(half_adder_21_carry));
  Half_adder half_adder_22 (
    .A(half_adder_13_sum), .B(half_adder_15_sum), .SUM(half_adder_22_sum), .CARRY(half_adder_22_carry));
  Half_adder half_adder_23 (
    .A(half_adder_13_carry), .B(half_adder_15_carry), .SUM(half_adder_23_sum), .CARRY(half_adder_23_carry));
  Half_adder half_adder_24 (
    .A(half_adder_14_carry), .B(half_adder_16_carry), .SUM(half_adder_24_sum), .CARRY(half_adder_24_carry));
  Half_adder half_adder_25 (
    .A(half_adder_17_sum), .B(half_adder_18_carry), .SUM(half_adder_25_sum), .CARRY(half_adder_25_carry));
  Half_adder half_adder_26 (
    .A(half_adder_18_sum), .B(half_adder_20_sum), .SUM(half_adder_26_sum), .CARRY(half_adder_26_carry));
  Half_adder half_adder_27 (.A(half_adder_19_sum), .B(half_adder_22_sum), .SUM(W1), .CARRY(half_adder_27_carry));
  Half_adder half_adder_28 (
    .A(half_adder_21_sum), .B(half_adder_23_sum), .SUM(half_adder_28_sum), .CARRY(half_adder_28_carry));
  Half_adder half_adder_29 (
    .A(half_adder_19_carry), .B(half_adder_22_carry), .SUM(half_adder_29_sum), .CARRY(half_adder_29_carry));
  Half_adder half_adder_30 (
    .A(half_adder_20_carry), .B(half_adder_21_carry), .SUM(half_adder_30_sum), .CARRY(half_adder_30_carry));
  Half_adder half_adder_31 (
    .A(half_adder_23_carry), .B(half_adder_24_sum), .SUM(half_adder_31_sum), .CARRY(half_adder_31_carry));
  Half_adder half_adder_32 (
    .A(half_adder_17_carry), .B(half_adder_24_carry), .SUM(half_adder_32_sum), .CARRY(half_adder_32_carry));
  Half_adder half_adder_33 (
    .A(half_adder_25_carry), .B(half_adder_30_carry), .SUM(half_adder_33_sum), .CARRY(half_adder_33_carry));
  Half_adder half_adder_34 (
    .A(half_adder_25_sum), .B(half_adder_26_carry), .SUM(half_adder_34_sum), .CARRY(half_adder_34_carry));
  Half_adder half_adder_35 (
    .A(half_adder_26_sum), .B(half_adder_29_sum), .SUM(half_adder_35_sum), .CARRY(half_adder_35_carry));
  Half_adder half_adder_36 (
    .A(half_adder_28_carry), .B(half_adder_29_carry), .SUM(half_adder_36_sum), .CARRY(half_adder_36_carry));
  Half_adder half_adder_37 (
    .A(half_adder_30_sum), .B(half_adder_31_sum), .SUM(half_adder_37_sum), .CARRY(half_adder_37_carry));
  Half_adder half_adder_38 (.A(half_adder_31_carry), .B(half_adder_32_carry), .SUM(half_adder_38_sum));  // open: CARRY
  Half_adder half_adder_39 (
    .A(half_adder_34_sum), .B(half_adder_41_sum), .SUM(half_adder_39_sum), .CARRY(half_adder_39_carry));
  Half_adder half_adder_40 (
    .A(half_adder_35_sum), .B(half_adder_27_carry), .SUM(half_adder_40_sum), .CARRY(half_adder_40_carry));
  Half_adder half_adder_41 (
    .A(half_adder_36_sum), .B(half_adder_37_sum), .SUM(half_adder_41_sum), .CARRY(half_adder_41_carry));
  Half_adder half_adder_42 (
    .A(half_adder_36_carry), .B(half_adder_37_carry), .SUM(half_adder_42_sum), .CARRY(half_adder_42_carry));
  Half_adder half_adder_43 (
    .A(half_adder_34_carry), .B(half_adder_39_carry), .SUM(half_adder_43_sum), .CARRY(half_adder_43_carry));
  Half_adder half_adder_44 (
    .A(half_adder_39_sum), .B(half_adder_45_carry), .SUM(half_adder_44_sum), .CARRY(half_adder_44_carry));
  Half_adder half_adder_45 (.A(half_adder_40_sum), .B(half_adder_28_sum), .SUM(W2), .CARRY(half_adder_45_carry));
  Half_adder half_adder_46 (
    .A(half_adder_41_carry), .B(half_adder_42_sum), .SUM(half_adder_46_sum), .CARRY(half_adder_46_carry));
  Half_adder half_adder_47 (.A(half_adder_42_carry), .B(half_adder_38_sum), .SUM(half_adder_47_sum));  // open: CARRY
  Half_adder half_adder_48 (.A(half_adder_43_carry), .B(half_adder_51_sum), .SUM(half_adder_48_sum));  // open: CARRY
  Half_adder half_adder_49 (
    .A(half_adder_43_sum), .B(half_adder_44_carry), .SUM(half_adder_49_sum), .CARRY(half_adder_49_carry));
  Half_adder half_adder_50 (
    .A(half_adder_44_sum), .B(half_adder_35_carry), .SUM(half_adder_50_sum), .CARRY(half_adder_50_carry));
  Half_adder half_adder_51 (.A(half_adder_46_carry), .B(half_adder_47_sum), .SUM(half_adder_51_sum));  // open: CARRY
  Half_adder half_adder_52 (.A(half_adder_48_sum), .B(half_adder_49_carry), .SUM(half_adder_52_sum));  // open: CARRY
  Half_adder half_adder_53 (
    .A(half_adder_49_sum), .B(half_adder_50_carry), .SUM(half_adder_53_sum), .CARRY(half_adder_53_carry));
  Half_adder half_adder_54 (.A(half_adder_50_sum), .B(half_adder_40_carry), .SUM(W4), .CARRY(half_adder_54_carry));
  Half_adder half_adder_55 (.A(half_adder_52_sum), .B(half_adder_53_carry), .SUM(half_adder_55_sum));  // open: CARRY
  Half_adder half_adder_56 (
    .A(half_adder_53_sum), .B(half_adder_54_carry), .SUM(half_adder_56_sum), .CARRY(half_adder_56_carry));
  Half_adder half_adder_57 (.A(half_adder_55_sum), .B(half_adder_56_carry), .SUM(half_adder_57_sum));  // open: CARRY
  Half_adder half_adder_58 (
    .A(half_adder_56_sum), .B(half_adder_46_sum), .SUM(half_adder_58_sum), .CARRY(half_adder_58_carry));
  Half_adder half_adder_59 (.A(half_adder_57_sum), .B(half_adder_58_carry), .SUM(half_adder_59_sum));  // open: CARRY
  Half_adder half_adder_60 (
    .A(half_adder_58_sum), .B(half_adder_32_sum), .SUM(half_adder_60_sum), .CARRY(half_adder_60_carry));
  Half_adder half_adder_61 (.A(half_adder_59_sum), .B(half_adder_60_carry), .SUM(half_adder_61_sum));  // open: CARRY
  Half_adder half_adder_62 (.A(half_adder_60_sum), .B(half_adder_33_sum), .SUM(W8), .CARRY(half_adder_62_carry));
  Half_adder half_adder_63 (.A(half_adder_61_sum), .B(half_adder_33_carry), .SUM(half_adder_63_sum));  // open: CARRY
  Half_adder half_adder_64 (.A(half_adder_63_sum), .B(half_adder_62_carry), .SUM(W16));  // open: CARRY
endmodule

module Decision_Maker (
  input  T8,
  input  T4,
  input  T2,
  input  T1,
  input  M8,
  input  M4,
  input  M2,
  input  M1,
  output M_ge_T
);

  wire and_1_out, and_2_out, and_3_out, and_4_out, and_5_out, and_6_out, and_7_out, and_8_out, and_9_out,
       and_10_out, and_11_out, and_12_out, and_13_out, and_14_out, and_15_out, and_16_out, and_17_out,
       and_18_out, not_1_out, not_2_out, not_3_out, not_4_out, or_1_out, or_2_out, xor_1_out, xor_2_out,
       xor_3_out, xor_4_out, xor_5_out, xor_6_out, xor_7_out, xor_8_out;

  and and_1 (and_1_out, T8, xor_1_out);
  xor xor_1 (xor_1_out, T8, M8);
  and and_2 (and_2_out, T4, xor_2_out);
  xor xor_2 (xor_2_out, T4, M4);
  xor xor_3 (xor_3_out, M8, T8);
  xor xor_4 (xor_4_out, M4, T4);
  not not_1 (not_1_out, and_1_out);
  not not_2 (not_2_out, and_2_out);
  and and_3 (and_3_out, M8, xor_3_out);
  and and_4 (and_4_out, not_2_out, and_5_out);
  and and_5 (and_5_out, M4, xor_4_out);
  and and_6 (and_6_out, not_1_out, and_3_out);
  and and_7 (and_7_out, not_1_out, and_4_out);
  xor xor_5 (xor_5_out, T2, M2);
  xor xor_6 (xor_6_out, T1, M1);
  xor xor_7 (xor_7_out, M2, T2);
  xor xor_8 (xor_8_out, M1, T1);
  and and_8 (and_8_out, T2, xor_5_out);
  and and_9 (and_9_out, T1, xor_6_out);
  and and_10 (and_10_out, M2, xor_7_out);
  and and_11 (and_11_out, M1, xor_8_out);
  not not_3 (not_3_out, and_8_out);
  not not_4 (not_4_out, and_9_out);
  or or_1 (or_1_out, and_6_out, and_7_out);
  and and_12 (and_12_out, not_3_out, and_10_out);
  and and_13 (and_13_out, and_12_out, not_1_out);
  or or_2 (or_2_out, and_15_out, or_1_out);
  and and_14 (and_14_out, not_4_out, and_11_out);
  and and_15 (and_15_out, and_13_out, not_2_out);
  or or_3 (M_ge_T, and_18_out, or_2_out);
  and and_16 (and_16_out, and_14_out, not_1_out);
  and and_17 (and_17_out, and_16_out, not_2_out);
  and and_18 (and_18_out, and_17_out, not_3_out);
endmodule

module Binary2BCD (
  input  I128,
  input  I64,
  input  I32,
  input  I16,
  input  I8,
  input  I4,
  input  I2,
  input  I1,
  output O1_8,
  output O1_4,
  output O1_2,
  output O1_1,
  output O2_8,
  output O2_4,
  output O2_2,
  output O2_1,
  output O3_8,
  output O3_4,
  output O3_2,
  output O3_1
);

  wire and_1_out, and_2_out, and_3_out, and_4_out, and_5_out, and_6_out, and_7_out, nand_1_out, nand_2_out,
       nand_3_out, nand_4_out, nand_5_out, nand_6_out, nand_7_out, nand_8_out, nand_9_out, nand_10_out,
       nand_11_out, nand_12_out, nand_13_out, nand_14_out, nand_15_out, nand_19_out, nand_20_out,
       nand_21_out, nand_22_out, nand_23_out, nand_24_out, nand_25_out, nand_26_out, nand_27_out,
       nand_28_out, nand_29_out, nand_31_out, nand_32_out, nand_33_out, nand_34_out, nand_35_out,
       nand_36_out, nand_37_out, nand_38_out, nand_39_out, nand_40_out, nand_41_out, nand_42_out,
       nand_43_out, nand_44_out, nand_45_out, nand_46_out, nand_47_out, nand_48_out, nand_49_out,
       nand_51_out, nand_52_out, nand_53_out, nand_54_out, nand_55_out, nand_56_out, nand_57_out,
       nand_58_out, nand_59_out, nand_60_out, nand_61_out, nand_62_out, nand_63_out, nand_67_out,
       nand_68_out, nand_69_out, nor_1_out, nor_2_out, nor_3_out, nor_4_out, nor_5_out, nor_6_out, nor_7_out,
       nor_8_out, nor_9_out, nor_10_out, nor_11_out, nor_12_out, nor_13_out, nor_14_out, not_1_out,
       not_2_out, not_3_out, not_4_out, not_5_out, not_6_out, not_7_out, not_8_out, not_9_out, not_10_out,
       not_11_out, not_12_out, not_13_out, not_14_out, or_1_out, or_2_out, or_3_out, or_4_out, or_5_out,
       or_6_out, or_7_out, or_8_out, or_9_out, or_10_out, or_11_out, or_12_out, or_13_out, or_14_out,
       or_15_out, or_16_out, or_17_out, or_18_out, or_19_out, or_20_out, or_21_out, or_22_out, or_23_out,
       or_24_out, or_25_out, or_26_out, or_27_out, or_28_out;

  nand nand_1 (nand_1_out, 1'b0, I32);
  nor nor_1 (nor_1_out, I128, 1'b0);
  and and_1 (and_1_out, I64, I128);
  not not_1 (not_1_out, I32);
  not not_2 (not_2_out, I128);
  nand nand_2 (nand_2_out, nand_62_out, I4);
  nor nor_2 (nor_2_out, nand_61_out, nand_62_out);
  and and_2 (and_2_out, nand_60_out, nand_61_out);
  not not_3 (not_3_out, I4);
  not not_4 (not_4_out, nand_61_out);
  nand nand_3 (nand_3_out, nand_24_out, I2);
  nor nor_3 (nor_3_out, nand_23_out, nand_24_out);
  and and_3 (and_3_out, nand_22_out, nand_23_out);
  not not_5 (not_5_out, I2);
  not not_6 (not_6_out, nand_23_out);
  nand nand_4 (nand_4_out, I128, not_1_out);
  nand nand_5 (nand_5_out, I32, nor_1_out);
  nor nor_4 (nor_4_out, 1'b0, and_1_out);
  nand nand_6 (nand_6_out, not_1_out, 1'b0);
  or or_1 (or_1_out, I64, not_2_out);
  nand nand_7 (nand_7_out, nand_61_out, not_3_out);
  nand nand_8 (nand_8_out, I4, nor_2_out);
  nor nor_5 (nor_5_out, nand_62_out, and_2_out);
  nand nand_9 (nand_9_out, not_3_out, nand_62_out);
  or or_2 (or_2_out, nand_60_out, not_4_out);
  nand nand_10 (nand_10_out, nand_23_out, not_5_out);
  nand nand_11 (nand_11_out, I2, nor_3_out);
  nor nor_6 (nor_6_out, nand_24_out, and_3_out);
  nand nand_12 (nand_12_out, not_5_out, nand_24_out);
  or or_3 (or_3_out, nand_22_out, not_6_out);
  nand nand_13 (nand_13_out, nand_4_out, I64);
  or or_4 (or_4_out, nor_4_out, I32);
  or or_5 (or_5_out, or_1_out, I32);
  nand nand_14 (nand_14_out, nand_7_out, nand_60_out);
  or or_6 (or_6_out, nor_5_out, I4);
  or or_7 (or_7_out, or_2_out, I4);
  nand nand_15 (nand_15_out, nand_10_out, nand_22_out);
  or or_8 (or_8_out, nor_6_out, I2);
  or or_9 (or_9_out, or_3_out, I2);
  nand nand_16 (O3_2, nand_11_out, or_8_out);
  nand nand_17 (O3_4, nand_15_out, nand_12_out);
  nand nand_18 (O3_8, nand_3_out, or_9_out);
  nand nand_19 (nand_19_out, nand_5_out, or_4_out);
  nand nand_20 (nand_20_out, nand_13_out, nand_6_out);
  nand nand_21 (nand_21_out, nand_1_out, or_5_out);
  nand nand_22 (nand_22_out, nand_8_out, or_6_out);
  nand nand_23 (nand_23_out, nand_14_out, nand_9_out);
  nand nand_24 (nand_24_out, nand_2_out, or_7_out);
  or or_10 (or_10_out, nand_19_out, not_1_out);
  nand nand_25 (nand_25_out, nand_19_out, not_1_out);
  or or_11 (or_11_out, nand_22_out, not_3_out);
  nand nand_26 (nand_26_out, nand_22_out, not_3_out);
  or or_12 (or_12_out, O3_2, not_5_out);
  nand nand_27 (nand_27_out, O3_2, not_5_out);
  nand nand_28 (nand_28_out, or_10_out, nand_25_out);
  nand nand_29 (nand_29_out, or_11_out, nand_26_out);
  nand nand_30 (O2_1, or_12_out, nand_27_out);
  nand nand_31 (nand_31_out, nand_21_out, I16);
  nor nor_7 (nor_7_out, nand_20_out, nand_21_out);
  and and_4 (and_4_out, nand_19_out, nand_20_out);
  not not_7 (not_7_out, I16);
  not not_8 (not_8_out, nand_20_out);
  nand nand_32 (nand_32_out, 1'b0, nand_68_out);
  nor nor_8 (nor_8_out, nand_28_out, 1'b0);
  and and_5 (and_5_out, nand_48_out, nand_28_out);
  not not_9 (not_9_out, nand_68_out);
  not not_10 (not_10_out, nand_28_out);
  nand nand_33 (nand_33_out, nand_20_out, not_7_out);
  nand nand_34 (nand_34_out, I16, nor_7_out);
  nor nor_9 (nor_9_out, nand_21_out, and_4_out);
  nand nand_35 (nand_35_out, not_7_out, nand_21_out);
  or or_13 (or_13_out, nand_19_out, not_8_out);
  nand nand_36 (nand_36_out, nand_28_out, not_9_out);
  nand nand_37 (nand_37_out, nand_68_out, nor_8_out);
  nor nor_10 (nor_10_out, 1'b0, and_5_out);
  nand nand_38 (nand_38_out, not_9_out, 1'b0);
  or or_14 (or_14_out, nand_48_out, not_10_out);
  nand nand_39 (nand_39_out, nand_33_out, nand_19_out);
  or or_15 (or_15_out, nor_9_out, I16);
  or or_16 (or_16_out, or_13_out, I16);
  nand nand_40 (nand_40_out, nand_36_out, nand_48_out);
  or or_17 (or_17_out, nor_10_out, nand_68_out);
  or or_18 (or_18_out, or_14_out, nand_68_out);
  nand nand_41 (nand_41_out, nand_34_out, or_15_out);
  nand nand_42 (nand_42_out, nand_39_out, nand_35_out);
  nand nand_43 (nand_43_out, nand_31_out, or_16_out);
  nand nand_44 (nand_44_out, nand_37_out, or_17_out);
  nand nand_45 (nand_45_out, nand_40_out, nand_38_out);
  nand nand_46 (nand_46_out, nand_32_out, or_18_out);
  or or_19 (or_19_out, nand_41_out, not_7_out);
  nand nand_47 (nand_47_out, nand_41_out, not_7_out);
  nand nand_48 (nand_48_out, or_19_out, nand_47_out);
  or or_20 (or_20_out, nand_44_out, not_9_out);
  nand nand_49 (nand_49_out, nand_44_out, not_9_out);
  nand nand_50 (O1_2, or_20_out, nand_49_out);
  nand nand_51 (nand_51_out, nand_43_out, I8);
  nor nor_11 (nor_11_out, nand_42_out, nand_43_out);
  and and_6 (and_6_out, nand_41_out, nand_42_out);
  not not_11 (not_11_out, I8);
  not not_12 (not_12_out, nand_42_out);
  nand nand_52 (nand_52_out, nand_46_out, nand_29_out);
  nor nor_12 (nor_12_out, nand_45_out, nand_46_out);
  and and_7 (and_7_out, nand_44_out, nand_45_out);
  not not_13 (not_13_out, nand_29_out);
  not not_14 (not_14_out, nand_45_out);
  nand nand_53 (nand_53_out, nand_42_out, not_11_out);
  nand nand_54 (nand_54_out, I8, nor_11_out);
  nor nor_13 (nor_13_out, nand_43_out, and_6_out);
  nand nand_55 (nand_55_out, not_11_out, nand_43_out);
  or or_21 (or_21_out, nand_41_out, not_12_out);
  nand nand_56 (nand_56_out, nand_45_out, not_13_out);
  nand nand_57 (nand_57_out, nand_29_out, nor_12_out);
  nor nor_14 (nor_14_out, nand_46_out, and_7_out);
  nand nand_58 (nand_58_out, not_13_out, nand_46_out);
  or or_22 (or_22_out, nand_44_out, not_14_out);
  nand nand_59 (nand_59_out, nand_53_out, nand_41_out);
  or or_23 (or_23_out, nor_13_out, I8);
  or or_24 (or_24_out, or_21_out, I8);
  or or_25 (or_25_out, nor_14_out, nand_29_out);
  or or_26 (or_26_out, or_22_out, nand_29_out);
  nand nand_60 (nand_60_out, nand_54_out, or_23_out);
  nand nand_61 (nand_61_out, nand_59_out, nand_55_out);
  nand nand_62 (nand_62_out, nand_51_out, or_24_out);
  nand nand_63 (nand_63_out, nand_56_out, nand_44_out);
  nand nand_64 (O2_2, nand_57_out, or_25_out);
  nand nand_65 (O2_4, nand_63_out, nand_58_out);
  nand nand_66 (O2_8, nand_52_out, or_26_out);
  or or_27 (or_27_out, nand_60_out, not_11_out);
  nand nand_67 (nand_67_out, nand_60_out, not_11_out);
  or or_28 (or_28_out, O2_2, not_13_out);
  nand nand_68 (nand_68_out, or_27_out, nand_67_out);
  nand nand_69 (nand_69_out, O2_2, not_13_out);
  nand nand_70 (O1_1, or_28_out, nand_69_out);

  assign O3_1 = I1;

  // Notes on the sheet:
  //   DABBLER T
  //   DABBLER D
  //   DABBLER N
  //   D2
  //   T3
  //   T2
  //   T1
  //   T0
  //   D3
  //   D1
  //   D0
  //   N3
  //   N2
  //   N1
  //   N0
  //   DABBLER W
  //   DABBLER K
  //   W2
  //   W1
  //   W3
  //   W0
  //   K3
  //   K2
  //   K1
  //   K0
  //   DABBLER Z
  //   DABBLER M
  //   M1
  //   M0
  //   Z3
  //   Z2
  //   Z1
  //   Z0
  //   M3
  //   M2
endmodule

module Segment_Display (
  input  D8,
  input  D4,
  input  D2,
  input  D1,
  output B,
  output A,
  output G,
  output F,
  output E,
  output D,
  output C
);

  wire and_1_out, and_2_out, and_3_out, and_4_out, nand_1_out, nand_2_out, nand_3_out, nand_4_out,
       nand_5_out, nor_1_out, nor_2_out, nor_3_out, not_1_out, not_2_out, not_3_out, not_4_out, not_5_out,
       not_6_out, not_7_out, or_1_out, or_2_out, or_3_out, or_5_out, or_6_out;

  not not_1 (not_1_out, D8);
  not not_2 (not_2_out, D4);
  not not_3 (not_3_out, D2);
  not not_4 (not_4_out, D1);
  and and_1 (and_1_out, not_1_out, not_2_out, not_3_out, not_4_out);
  nor nor_1 (nor_1_out, D8, D2);
  not not_5 (not_5_out, D2);
  nand nand_1 (nand_1_out, D1, D2);
  nor nor_2 (nor_2_out, D1, D2);
  or or_1 (or_1_out, D1, nor_1_out);
  and and_2 (and_2_out, D4, nand_1_out);
  or or_2 (or_2_out, not_5_out, D4);
  nand nand_2 (nand_2_out, not_5_out, D4);
  not not_6 (not_6_out, or_1_out);
  or or_3 (or_3_out, D8, and_2_out);
  nor nor_3 (nor_3_out, nand_2_out, D1);
  and and_3 (and_3_out, D1, nand_2_out);
  not not_7 (not_7_out, or_3_out);
  nand nand_3 (nand_3_out, D1, or_3_out);
  or or_4 (C, or_3_out, and_1_out, and_3_out);
  or or_5 (or_5_out, or_3_out, nor_2_out);
  and and_4 (and_4_out, nand_3_out, or_2_out);
  nand nand_4 (nand_4_out, and_4_out, or_1_out);
  or or_6 (or_6_out, not_7_out, nand_4_out);
  or or_7 (A, D2, and_1_out, nand_4_out);
  or or_8 (G, nand_4_out, nor_3_out);
  nand nand_5 (nand_5_out, or_6_out, or_5_out);
  or or_9 (B, D8, and_1_out, nand_5_out);
  or or_10 (F, or_3_out, and_1_out);
  or or_11 (D, and_1_out, nand_4_out);
  or or_12 (E, and_1_out, not_6_out);
endmodule

module Super_System (
  input  T8,
  input  T4,
  input  T2,
  input  T1,
  input  I1,
  input  I2,
  input  I3,
  input  I4,
  input  I5,
  input  I6,
  input  I7,
  input  I8,
  input  I9,
  input  I10,
  input  I11,
  input  I12,
  input  I13,
  input  I14,
  input  I15,
  input  I16,
  input  cnvd_rst,
  input  ad_seq,
  input  clr_sf,
  input  rst_haz_track,
  output MPB,
  output MPA,
  output MPG,
  output MPF,
  output MPE,
  output MPD,
  output MPC,
  output PB,
  output PA,
  output PG,
  output PF,
  output PE,
  output PD,
  output PC,
  output RECOGNITION,
  output ad_seq_success,
  output MTB,
  output MTA,
  output MTG,
  output MTF,
  output MTE,
  output MTD,
  output MTC,
  output TB,
  output TA,
  output TG,
  output TF,
  output TE,
  output TD,
  output TC,
  output rearm_seq,
  output tim_haz_det,
  output Haz_nul
);

  wire and_1_out, and_2_out, and_3_out, and_4_out, binary2bcd_1_o2_1, binary2bcd_1_o2_2, binary2bcd_1_o2_4,
       binary2bcd_1_o2_8, binary2bcd_1_o3_1, binary2bcd_1_o3_2, binary2bcd_1_o3_4, binary2bcd_1_o3_8,
       binary2bcd_2_o2_1, binary2bcd_2_o2_2, binary2bcd_2_o2_4, binary2bcd_2_o2_8, binary2bcd_2_o3_1,
       binary2bcd_2_o3_2, binary2bcd_2_o3_4, binary2bcd_2_o3_8, d_ff_1_q, d_ff_2_q, d_ff_3_q, d_ff_4_q,
       decision_maker_1_m_ge_t, not_1_out, not_2_out, not_3_out, or_2_out, or_3_out, or_4_out, or_5_out,
       pop_counter_1_w1, pop_counter_1_w2, pop_counter_1_w4, pop_counter_1_w8, pop_counter_1_w16, undriven,
       undriven_2, undriven_3, undriven_4, undriven_5, undriven_6, undriven_7;

  POP_Counter pop_counter_1 (
    .I1(I1), .I2(I2), .I3(I3), .I4(I4), .I5(I5), .I6(I6), .I7(I7), .I8(I8), .I9(I9), .I10(I10), .I11(I11),
    .I12(I12), .I13(I13), .I14(I14), .I15(I15), .I16(I16), .W16(pop_counter_1_w16), .W8(pop_counter_1_w8),
    .W4(pop_counter_1_w4), .W2(pop_counter_1_w2), .W1(pop_counter_1_w1));
  // NoConnect on undriven
  // NoConnect on undriven_2
  // NoConnect on undriven_3
  // NoConnect on undriven_4
  // NoConnect on undriven_5
  // NoConnect on undriven_6
  // NoConnect on undriven_7
  Binary2BCD binary2bcd_1 (
    .I128(undriven), .I64(undriven_2), .I32(undriven_3), .I16(pop_counter_1_w16), .I8(pop_counter_1_w8),
    .I4(pop_counter_1_w4), .I2(pop_counter_1_w2), .I1(pop_counter_1_w1), .O2_8(binary2bcd_1_o2_8),
    .O2_4(binary2bcd_1_o2_4), .O2_2(binary2bcd_1_o2_2), .O2_1(binary2bcd_1_o2_1), .O3_8(binary2bcd_1_o3_8),
    .O3_4(binary2bcd_1_o3_4), .O3_2(binary2bcd_1_o3_2), .O3_1(binary2bcd_1_o3_1));  // open: O1_8, O1_4, O1_2, O1_1
  Decision_Maker decision_maker_1 (
    .T8(T8), .T4(T4), .T2(T2), .T1(T1), .M8(pop_counter_1_w8), .M4(pop_counter_1_w4), .M2(pop_counter_1_w2),
    .M1(pop_counter_1_w1), .M_ge_T(decision_maker_1_m_ge_t));
  Binary2BCD binary2bcd_2 (
    .I128(undriven_4), .I64(undriven_5), .I32(undriven_6), .I16(undriven_7), .I8(T8), .I4(T4), .I2(T2),
    .I1(T1), .O2_8(binary2bcd_2_o2_8), .O2_4(binary2bcd_2_o2_4), .O2_2(binary2bcd_2_o2_2),
    .O2_1(binary2bcd_2_o2_1), .O3_8(binary2bcd_2_o3_8), .O3_4(binary2bcd_2_o3_4), .O3_2(binary2bcd_2_o3_2),
    .O3_1(binary2bcd_2_o3_1));  // open: O1_8, O1_4, O1_2, O1_1
  or or_1 (RECOGNITION, decision_maker_1_m_ge_t, pop_counter_1_w16);
  D_Flip_Flop d_ff_1 (.D(RECOGNITION), .clk(RECOGNITION), .Q(d_ff_1_q), .reset(or_3_out));  // open: Qn, preset
  not not_1 (not_1_out, RECOGNITION);
  D_Flip_Flop d_ff_2 (.D(not_1_out), .clk(not_1_out), .Q(d_ff_2_q), .reset(or_3_out));  // open: Qn, preset
  Segment_Display segment_display_1 (
    .D8(binary2bcd_1_o2_8), .D4(binary2bcd_1_o2_4), .D2(binary2bcd_1_o2_2), .D1(binary2bcd_1_o2_1), .B(MPB),
    .A(MPA), .G(MPG), .F(MPF), .E(MPE), .D(MPD), .C(MPC));
  Segment_Display segment_display_2 (
    .D8(binary2bcd_1_o3_8), .D4(binary2bcd_1_o3_4), .D2(binary2bcd_1_o3_2), .D1(binary2bcd_1_o3_1), .B(PB),
    .A(PA), .G(PG), .F(PF), .E(PE), .D(PD), .C(PC));
  Segment_Display segment_display_3 (
    .D8(binary2bcd_2_o2_8), .D4(binary2bcd_2_o2_4), .D2(binary2bcd_2_o2_2), .D1(binary2bcd_2_o2_1), .B(MTB),
    .A(MTA), .G(MTG), .F(MTF), .E(MTE), .D(MTD), .C(MTC));
  Segment_Display segment_display_4 (
    .D8(binary2bcd_2_o3_8), .D4(binary2bcd_2_o3_4), .D2(binary2bcd_2_o3_2), .D1(binary2bcd_2_o3_1), .B(TB),
    .A(TA), .G(TG), .F(TF), .E(TE), .D(TD), .C(TC));
  and and_1 (and_1_out, and_4_out, ad_seq);
  D_Flip_Flop d_ff_3 (.D(and_2_out), .clk(d_ff_1_q), .Q(d_ff_3_q), .reset(or_2_out));  // open: Qn, preset
  and and_2 (and_2_out, 1'b1, ad_seq);
  D_Flip_Flop d_ff_4 (.D(and_3_out), .clk(d_ff_2_q), .Q(d_ff_4_q), .reset(or_2_out));  // open: Qn, preset
  and and_3 (and_3_out, 1'b1, ad_seq);
  and and_4 (and_4_out, d_ff_1_q, d_ff_2_q);
  or or_2 (or_2_out, and_4_out, cnvd_rst);
  D_Flip_Flop d_ff_5 (.D(and_1_out), .clk(and_1_out), .Q(tim_haz_det), .reset(rst_haz_track));  // open: Qn, preset
  or or_3 (or_3_out, or_2_out, not_2_out);
  or or_4 (or_4_out, and_4_out, clr_sf);
  D_Flip_Flop d_ff_6 (.D(1'b1), .clk(or_5_out), .Q(ad_seq_success), .reset(or_4_out));  // open: Qn, preset
  or or_5 (or_5_out, d_ff_3_q, d_ff_4_q);
  not not_2 (not_2_out, ad_seq);
  and and_5 (Haz_nul, tim_haz_det, not_3_out);
  not not_3 (not_3_out, and_1_out);

  assign rearm_seq = ad_seq_success;

  // Notes on the sheet:
  //   T-PINS (SET THE THRESHOLD)
  //   RECOGNIZED
  //   MATCHED-PIXELS
  //   THRESHOLD
endmodule

module single_thresh_storage (
  input  D1,
  input  D2,
  input  D3,
  input  D4,
  input  WR,
  input  RESET,
  input  EN,
  output V1,
  output V2,
  output V3,
  output V4,
  output CLK,
  output O1,
  output O2,
  output O3,
  output O4
);

  wire controlled_buffer_1_out, controlled_buffer_2_out, controlled_buffer_3_out, controlled_buffer_4_out,
       d_ff_1_qn, d_ff_2_qn, d_ff_3_qn, d_ff_4_qn;

  assign controlled_buffer_1_out = WR ? D1 : 1'bz;  // Controlled_Buffer controlled_buffer_1
  assign controlled_buffer_2_out = WR ? D2 : 1'bz;  // Controlled_Buffer controlled_buffer_2
  D_Flip_Flop d_ff_1 (.D(controlled_buffer_1_out), .clk(CLK), .Q(V1), .Qn(d_ff_1_qn), .reset(RESET));  // open: preset
  Clock clock_1 (.out(CLK));
  assign controlled_buffer_3_out = WR ? D3 : 1'bz;  // Controlled_Buffer controlled_buffer_3
  D_Flip_Flop d_ff_2 (.D(controlled_buffer_2_out), .clk(CLK), .Q(V2), .Qn(d_ff_2_qn), .reset(RESET));  // open: preset
  assign O1 = EN ? ~d_ff_1_qn : 1'bz;  // Controlled_Inverter controlled_inverter_1
  assign controlled_buffer_4_out = WR ? D4 : 1'bz;  // Controlled_Buffer controlled_buffer_4
  D_Flip_Flop d_ff_3 (.D(controlled_buffer_3_out), .clk(CLK), .Q(V3), .Qn(d_ff_3_qn), .reset(RESET));  // open: preset
  D_Flip_Flop d_ff_4 (.D(controlled_buffer_4_out), .clk(CLK), .Q(V4), .Qn(d_ff_4_qn), .reset(RESET));  // open: preset
  assign O2 = EN ? ~d_ff_2_qn : 1'bz;  // Controlled_Inverter controlled_inverter_2
  assign O3 = EN ? ~d_ff_3_qn : 1'bz;  // Controlled_Inverter controlled_inverter_3
  assign O4 = EN ? ~d_ff_4_qn : 1'bz;  // Controlled_Inverter controlled_inverter_4
endmodule

module thresh_memory (
  input  RESET,
  input  Mem_Prog_EN,
  input  D1,
  input  D2,
  input  D4,
  input  D8,
  input  A1,
  input  A2,
  input  A4,
  input  A8,
  input  CHIP_EN,
  input  E0W1,
  output O1,
  output O2,
  output O4,
  output O8
);

  wire address_decode_logic_1_cell_0_e, address_decode_logic_1_cell_0_w, address_decode_logic_1_cell_1_e,
       address_decode_logic_1_cell_1_w, address_decode_logic_1_cell_2_e, address_decode_logic_1_cell_2_w,
       address_decode_logic_1_cell_3_e, address_decode_logic_1_cell_3_w, address_decode_logic_1_cell_4_e,
       address_decode_logic_1_cell_4_w, address_decode_logic_1_cell_5_e, address_decode_logic_1_cell_5_w,
       address_decode_logic_1_cell_6_e, address_decode_logic_1_cell_6_w, address_decode_logic_1_cell_7_e,
       address_decode_logic_1_cell_7_w, address_decode_logic_1_cell_8_e, address_decode_logic_1_cell_8_w,
       address_decode_logic_1_cell_9_e, address_decode_logic_1_cell_9_w, address_decode_logic_1_cell_10_e,
       address_decode_logic_1_cell_10_w, address_decode_logic_1_cell_11_e, address_decode_logic_1_cell_11_w,
       address_decode_logic_1_cell_12_e, address_decode_logic_1_cell_12_w, address_decode_logic_1_cell_13_e,
       address_decode_logic_1_cell_13_w, address_decode_logic_1_cell_14_e, address_decode_logic_1_cell_14_w,
       address_decode_logic_1_cell_15_e, address_decode_logic_1_cell_15_w, single_thresh_storage_1_clk,
       single_thresh_storage_1_v1, single_thresh_storage_1_v2, single_thresh_storage_1_v3,
       single_thresh_storage_1_v4, single_thresh_storage_2_clk, single_thresh_storage_2_v1,
       single_thresh_storage_2_v2, single_thresh_storage_2_v3, single_thresh_storage_2_v4,
       single_thresh_storage_3_clk, single_thresh_storage_3_v1, single_thresh_storage_3_v2,
       single_thresh_storage_3_v3, single_thresh_storage_3_v4, single_thresh_storage_4_clk,
       single_thresh_storage_4_v1, single_thresh_storage_4_v2, single_thresh_storage_4_v3,
       single_thresh_storage_4_v4, single_thresh_storage_5_clk, single_thresh_storage_5_v1,
       single_thresh_storage_5_v2, single_thresh_storage_5_v3, single_thresh_storage_5_v4,
       single_thresh_storage_6_clk, single_thresh_storage_6_v1, single_thresh_storage_6_v2,
       single_thresh_storage_6_v3, single_thresh_storage_6_v4, single_thresh_storage_7_clk,
       single_thresh_storage_7_v1, single_thresh_storage_7_v2, single_thresh_storage_7_v3,
       single_thresh_storage_7_v4, single_thresh_storage_8_clk, single_thresh_storage_8_v1,
       single_thresh_storage_8_v2, single_thresh_storage_8_v3, single_thresh_storage_8_v4,
       single_thresh_storage_9_clk, single_thresh_storage_9_v1, single_thresh_storage_9_v2,
       single_thresh_storage_9_v3, single_thresh_storage_9_v4, single_thresh_storage_10_clk,
       single_thresh_storage_10_v1, single_thresh_storage_10_v2, single_thresh_storage_10_v3,
       single_thresh_storage_10_v4, single_thresh_storage_11_clk, single_thresh_storage_11_v1,
       single_thresh_storage_11_v2, single_thresh_storage_11_v3, single_thresh_storage_11_v4,
       single_thresh_storage_12_clk, single_thresh_storage_12_v1, single_thresh_storage_12_v2,
       single_thresh_storage_12_v3, single_thresh_storage_12_v4, single_thresh_storage_13_clk,
       single_thresh_storage_13_v1, single_thresh_storage_13_v2, single_thresh_storage_13_v3,
       single_thresh_storage_13_v4, single_thresh_storage_14_clk, single_thresh_storage_14_v1,
       single_thresh_storage_14_v2, single_thresh_storage_14_v3, single_thresh_storage_14_v4,
       single_thresh_storage_15_clk, single_thresh_storage_15_v1, single_thresh_storage_15_v2,
       single_thresh_storage_15_v3, single_thresh_storage_15_v4, single_thresh_storage_16_clk,
       single_thresh_storage_16_v1, single_thresh_storage_16_v2, single_thresh_storage_16_v3,
       single_thresh_storage_16_v4;

  address_decode_logic address_decode_logic_1 (
    .A0(A1), .A1(A2), .A2(A4), .A3(A8), .OUT_CONTROL(CHIP_EN), .E0W1(E0W1),
    .CELL_0_E(address_decode_logic_1_cell_0_e), .CELL_0_W(address_decode_logic_1_cell_0_w),
    .CELL_1_E(address_decode_logic_1_cell_1_e), .CELL_1_W(address_decode_logic_1_cell_1_w),
    .CELL_2_E(address_decode_logic_1_cell_2_e), .CELL_2_W(address_decode_logic_1_cell_2_w),
    .CELL_3_E(address_decode_logic_1_cell_3_e), .CELL_3_W(address_decode_logic_1_cell_3_w),
    .CELL_4_E(address_decode_logic_1_cell_4_e), .CELL_4_W(address_decode_logic_1_cell_4_w),
    .CELL_5_E(address_decode_logic_1_cell_5_e), .CELL_5_W(address_decode_logic_1_cell_5_w),
    .CELL_6_E(address_decode_logic_1_cell_6_e), .CELL_6_W(address_decode_logic_1_cell_6_w),
    .CELL_7_E(address_decode_logic_1_cell_7_e), .CELL_7_W(address_decode_logic_1_cell_7_w),
    .CELL_8_E(address_decode_logic_1_cell_8_e), .CELL_8_W(address_decode_logic_1_cell_8_w),
    .CELL_9_E(address_decode_logic_1_cell_9_e), .CELL_9_W(address_decode_logic_1_cell_9_w),
    .CELL_10_E(address_decode_logic_1_cell_10_e), .CELL_10_W(address_decode_logic_1_cell_10_w),
    .CELL_11_E(address_decode_logic_1_cell_11_e), .CELL_11_W(address_decode_logic_1_cell_11_w),
    .CELL_12_E(address_decode_logic_1_cell_12_e), .CELL_12_W(address_decode_logic_1_cell_12_w),
    .CELL_13_E(address_decode_logic_1_cell_13_e), .CELL_13_W(address_decode_logic_1_cell_13_w),
    .CELL_14_E(address_decode_logic_1_cell_14_e), .CELL_14_W(address_decode_logic_1_cell_14_w),
    .CELL_15_E(address_decode_logic_1_cell_15_e), .CELL_15_W(address_decode_logic_1_cell_15_w));
  assign O1 = Mem_Prog_EN ? D1 : 1'bz;  // Controlled_Buffer controlled_buffer_1
  assign O2 = Mem_Prog_EN ? D2 : 1'bz;  // Controlled_Buffer controlled_buffer_2
  assign O4 = Mem_Prog_EN ? D4 : 1'bz;  // Controlled_Buffer controlled_buffer_3
  assign O8 = Mem_Prog_EN ? D8 : 1'bz;  // Controlled_Buffer controlled_buffer_4
  LED led_1 (.in(single_thresh_storage_1_v1));
  single_thresh_storage single_thresh_storage_1 (
    .D1(O1), .D2(O2), .D3(O4), .D4(O8), .WR(address_decode_logic_1_cell_0_w), .RESET(RESET),
    .EN(address_decode_logic_1_cell_0_e), .V1(single_thresh_storage_1_v1), .V2(single_thresh_storage_1_v2),
    .V3(single_thresh_storage_1_v3), .V4(single_thresh_storage_1_v4), .CLK(single_thresh_storage_1_clk),
    .O1(O1), .O2(O2), .O3(O4), .O4(O8));
  LED led_2 (.in(single_thresh_storage_1_v2));
  LED led_3 (.in(single_thresh_storage_1_v3));
  LED led_4 (.in(single_thresh_storage_1_v4));
  LED led_5 (.in(single_thresh_storage_1_clk));
  LED led_6 (.in(single_thresh_storage_2_v1));
  single_thresh_storage single_thresh_storage_2 (
    .D1(O1), .D2(O2), .D3(O4), .D4(O8), .WR(address_decode_logic_1_cell_4_w), .RESET(RESET),
    .EN(address_decode_logic_1_cell_4_e), .V1(single_thresh_storage_2_v1), .V2(single_thresh_storage_2_v2),
    .V3(single_thresh_storage_2_v3), .V4(single_thresh_storage_2_v4), .CLK(single_thresh_storage_2_clk),
    .O1(O1), .O2(O2), .O3(O4), .O4(O8));
  LED led_7 (.in(single_thresh_storage_2_v2));
  LED led_8 (.in(single_thresh_storage_2_v3));
  LED led_9 (.in(single_thresh_storage_2_v4));
  LED led_10 (.in(single_thresh_storage_2_clk));
  LED led_11 (.in(single_thresh_storage_3_v1));
  single_thresh_storage single_thresh_storage_3 (
    .D1(O1), .D2(O2), .D3(O4), .D4(O8), .WR(address_decode_logic_1_cell_8_w), .RESET(RESET),
    .EN(address_decode_logic_1_cell_8_e), .V1(single_thresh_storage_3_v1), .V2(single_thresh_storage_3_v2),
    .V3(single_thresh_storage_3_v3), .V4(single_thresh_storage_3_v4), .CLK(single_thresh_storage_3_clk),
    .O1(O1), .O2(O2), .O3(O4), .O4(O8));
  LED led_12 (.in(single_thresh_storage_3_v2));
  LED led_13 (.in(single_thresh_storage_3_v3));
  LED led_14 (.in(single_thresh_storage_3_v4));
  LED led_15 (.in(single_thresh_storage_3_clk));
  LED led_16 (.in(single_thresh_storage_4_v1));
  single_thresh_storage single_thresh_storage_4 (
    .D1(O1), .D2(O2), .D3(O4), .D4(O8), .WR(address_decode_logic_1_cell_12_w), .RESET(RESET),
    .EN(address_decode_logic_1_cell_12_e), .V1(single_thresh_storage_4_v1), .V2(single_thresh_storage_4_v2),
    .V3(single_thresh_storage_4_v3), .V4(single_thresh_storage_4_v4), .CLK(single_thresh_storage_4_clk),
    .O1(O1), .O2(O2), .O3(O4), .O4(O8));
  LED led_17 (.in(single_thresh_storage_4_v2));
  LED led_18 (.in(single_thresh_storage_4_v3));
  LED led_19 (.in(single_thresh_storage_4_v4));
  LED led_20 (.in(single_thresh_storage_4_clk));
  LED led_21 (.in(single_thresh_storage_5_v1));
  single_thresh_storage single_thresh_storage_5 (
    .D1(O1), .D2(O2), .D3(O4), .D4(O8), .WR(address_decode_logic_1_cell_1_w), .RESET(RESET),
    .EN(address_decode_logic_1_cell_1_e), .V1(single_thresh_storage_5_v1), .V2(single_thresh_storage_5_v2),
    .V3(single_thresh_storage_5_v3), .V4(single_thresh_storage_5_v4), .CLK(single_thresh_storage_5_clk),
    .O1(O1), .O2(O2), .O3(O4), .O4(O8));
  LED led_22 (.in(single_thresh_storage_5_v2));
  LED led_23 (.in(single_thresh_storage_5_v3));
  LED led_24 (.in(single_thresh_storage_5_v4));
  LED led_25 (.in(single_thresh_storage_5_clk));
  LED led_26 (.in(single_thresh_storage_6_v1));
  single_thresh_storage single_thresh_storage_6 (
    .D1(O1), .D2(O2), .D3(O4), .D4(O8), .WR(address_decode_logic_1_cell_5_w), .RESET(RESET),
    .EN(address_decode_logic_1_cell_5_e), .V1(single_thresh_storage_6_v1), .V2(single_thresh_storage_6_v2),
    .V3(single_thresh_storage_6_v3), .V4(single_thresh_storage_6_v4), .CLK(single_thresh_storage_6_clk),
    .O1(O1), .O2(O2), .O3(O4), .O4(O8));
  LED led_27 (.in(single_thresh_storage_6_v2));
  LED led_28 (.in(single_thresh_storage_6_v3));
  LED led_29 (.in(single_thresh_storage_6_v4));
  LED led_30 (.in(single_thresh_storage_6_clk));
  LED led_31 (.in(single_thresh_storage_7_v1));
  single_thresh_storage single_thresh_storage_7 (
    .D1(O1), .D2(O2), .D3(O4), .D4(O8), .WR(address_decode_logic_1_cell_9_w), .RESET(RESET),
    .EN(address_decode_logic_1_cell_9_e), .V1(single_thresh_storage_7_v1), .V2(single_thresh_storage_7_v2),
    .V3(single_thresh_storage_7_v3), .V4(single_thresh_storage_7_v4), .CLK(single_thresh_storage_7_clk),
    .O1(O1), .O2(O2), .O3(O4), .O4(O8));
  LED led_32 (.in(single_thresh_storage_7_v2));
  LED led_33 (.in(single_thresh_storage_7_v3));
  LED led_34 (.in(single_thresh_storage_7_v4));
  LED led_35 (.in(single_thresh_storage_7_clk));
  LED led_36 (.in(single_thresh_storage_8_v1));
  single_thresh_storage single_thresh_storage_8 (
    .D1(O1), .D2(O2), .D3(O4), .D4(O8), .WR(address_decode_logic_1_cell_13_w), .RESET(RESET),
    .EN(address_decode_logic_1_cell_13_e), .V1(single_thresh_storage_8_v1), .V2(single_thresh_storage_8_v2),
    .V3(single_thresh_storage_8_v3), .V4(single_thresh_storage_8_v4), .CLK(single_thresh_storage_8_clk),
    .O1(O1), .O2(O2), .O3(O4), .O4(O8));
  LED led_37 (.in(single_thresh_storage_8_v2));
  LED led_38 (.in(single_thresh_storage_8_v3));
  LED led_39 (.in(single_thresh_storage_8_v4));
  LED led_40 (.in(single_thresh_storage_8_clk));
  LED led_41 (.in(single_thresh_storage_9_v1));
  single_thresh_storage single_thresh_storage_9 (
    .D1(O1), .D2(O2), .D3(O4), .D4(O8), .WR(address_decode_logic_1_cell_2_w), .RESET(RESET),
    .EN(address_decode_logic_1_cell_2_e), .V1(single_thresh_storage_9_v1), .V2(single_thresh_storage_9_v2),
    .V3(single_thresh_storage_9_v3), .V4(single_thresh_storage_9_v4), .CLK(single_thresh_storage_9_clk),
    .O1(O1), .O2(O2), .O3(O4), .O4(O8));
  LED led_42 (.in(single_thresh_storage_9_v2));
  LED led_43 (.in(single_thresh_storage_9_v3));
  LED led_44 (.in(single_thresh_storage_9_v4));
  LED led_45 (.in(single_thresh_storage_9_clk));
  LED led_46 (.in(single_thresh_storage_10_v1));
  single_thresh_storage single_thresh_storage_10 (
    .D1(O1), .D2(O2), .D3(O4), .D4(O8), .WR(address_decode_logic_1_cell_6_w), .RESET(RESET),
    .EN(address_decode_logic_1_cell_6_e), .V1(single_thresh_storage_10_v1), .V2(single_thresh_storage_10_v2),
    .V3(single_thresh_storage_10_v3), .V4(single_thresh_storage_10_v4), .CLK(single_thresh_storage_10_clk),
    .O1(O1), .O2(O2), .O3(O4), .O4(O8));
  LED led_47 (.in(single_thresh_storage_10_v2));
  LED led_48 (.in(single_thresh_storage_10_v3));
  LED led_49 (.in(single_thresh_storage_10_v4));
  LED led_50 (.in(single_thresh_storage_10_clk));
  LED led_51 (.in(single_thresh_storage_11_v1));
  single_thresh_storage single_thresh_storage_11 (
    .D1(O1), .D2(O2), .D3(O4), .D4(O8), .WR(address_decode_logic_1_cell_10_w), .RESET(RESET),
    .EN(address_decode_logic_1_cell_10_e), .V1(single_thresh_storage_11_v1),
    .V2(single_thresh_storage_11_v2), .V3(single_thresh_storage_11_v3), .V4(single_thresh_storage_11_v4),
    .CLK(single_thresh_storage_11_clk), .O1(O1), .O2(O2), .O3(O4), .O4(O8));
  LED led_52 (.in(single_thresh_storage_11_v2));
  LED led_53 (.in(single_thresh_storage_11_v3));
  LED led_54 (.in(single_thresh_storage_11_v4));
  LED led_55 (.in(single_thresh_storage_11_clk));
  LED led_56 (.in(single_thresh_storage_12_v1));
  single_thresh_storage single_thresh_storage_12 (
    .D1(O1), .D2(O2), .D3(O4), .D4(O8), .WR(address_decode_logic_1_cell_14_w), .RESET(RESET),
    .EN(address_decode_logic_1_cell_14_e), .V1(single_thresh_storage_12_v1),
    .V2(single_thresh_storage_12_v2), .V3(single_thresh_storage_12_v3), .V4(single_thresh_storage_12_v4),
    .CLK(single_thresh_storage_12_clk), .O1(O1), .O2(O2), .O3(O4), .O4(O8));
  LED led_57 (.in(single_thresh_storage_12_v2));
  LED led_58 (.in(single_thresh_storage_12_v3));
  LED led_59 (.in(single_thresh_storage_12_v4));
  LED led_60 (.in(single_thresh_storage_12_clk));
  LED led_61 (.in(single_thresh_storage_13_v1));
  single_thresh_storage single_thresh_storage_13 (
    .D1(O1), .D2(O2), .D3(O4), .D4(O8), .WR(address_decode_logic_1_cell_3_w),
    .EN(address_decode_logic_1_cell_3_e), .V1(single_thresh_storage_13_v1), .V2(single_thresh_storage_13_v2),
    .V3(single_thresh_storage_13_v3), .V4(single_thresh_storage_13_v4), .CLK(single_thresh_storage_13_clk),
    .O1(O1), .O2(O2), .O3(O4), .O4(O8));  // open: RESET
  LED led_62 (.in(single_thresh_storage_13_v2));
  LED led_63 (.in(single_thresh_storage_13_v3));
  LED led_64 (.in(single_thresh_storage_13_v4));
  LED led_65 (.in(single_thresh_storage_13_clk));
  LED led_66 (.in(single_thresh_storage_14_v1));
  single_thresh_storage single_thresh_storage_14 (
    .D1(O1), .D2(O2), .D3(O4), .D4(O8), .WR(address_decode_logic_1_cell_7_w), .RESET(RESET),
    .EN(address_decode_logic_1_cell_7_e), .V1(single_thresh_storage_14_v1), .V2(single_thresh_storage_14_v2),
    .V3(single_thresh_storage_14_v3), .V4(single_thresh_storage_14_v4), .CLK(single_thresh_storage_14_clk),
    .O1(O1), .O2(O2), .O3(O4), .O4(O8));
  LED led_67 (.in(single_thresh_storage_14_v2));
  LED led_68 (.in(single_thresh_storage_14_v3));
  LED led_69 (.in(single_thresh_storage_14_v4));
  LED led_70 (.in(single_thresh_storage_14_clk));
  LED led_71 (.in(single_thresh_storage_15_v1));
  single_thresh_storage single_thresh_storage_15 (
    .D1(O1), .D2(O2), .D3(O4), .D4(O8), .WR(address_decode_logic_1_cell_11_w), .RESET(RESET),
    .EN(address_decode_logic_1_cell_11_e), .V1(single_thresh_storage_15_v1),
    .V2(single_thresh_storage_15_v2), .V3(single_thresh_storage_15_v3), .V4(single_thresh_storage_15_v4),
    .CLK(single_thresh_storage_15_clk), .O1(O1), .O2(O2), .O3(O4), .O4(O8));
  LED led_72 (.in(single_thresh_storage_15_v2));
  LED led_73 (.in(single_thresh_storage_15_v3));
  LED led_74 (.in(single_thresh_storage_15_v4));
  LED led_75 (.in(single_thresh_storage_15_clk));
  LED led_76 (.in(single_thresh_storage_16_v1));
  single_thresh_storage single_thresh_storage_16 (
    .D1(O1), .D2(O2), .D3(O4), .D4(O8), .WR(address_decode_logic_1_cell_15_w), .RESET(RESET),
    .EN(address_decode_logic_1_cell_15_e), .V1(single_thresh_storage_16_v1),
    .V2(single_thresh_storage_16_v2), .V3(single_thresh_storage_16_v3), .V4(single_thresh_storage_16_v4),
    .CLK(single_thresh_storage_16_clk), .O1(O1), .O2(O2), .O3(O4), .O4(O8));
  LED led_77 (.in(single_thresh_storage_16_v2));
  LED led_78 (.in(single_thresh_storage_16_v3));
  LED led_79 (.in(single_thresh_storage_16_v4));
  LED led_80 (.in(single_thresh_storage_16_clk));
endmodule

module address_decode_logic (
  input  A0,
  input  A1,
  input  A2,
  input  A3,
  input  OUT_CONTROL,
  input  E0W1,
  output CELL_0_E,
  output CELL_0_W,
  output CELL_1_E,
  output CELL_1_W,
  output CELL_2_E,
  output CELL_2_W,
  output CELL_3_E,
  output CELL_3_W,
  output CELL_4_E,
  output CELL_4_W,
  output CELL_5_E,
  output CELL_5_W,
  output CELL_6_E,
  output CELL_6_W,
  output CELL_7_E,
  output CELL_7_W,
  output CELL_8_E,
  output CELL_8_W,
  output CELL_9_E,
  output CELL_9_W,
  output CELL_10_E,
  output CELL_10_W,
  output CELL_11_E,
  output CELL_11_W,
  output CELL_12_E,
  output CELL_12_W,
  output CELL_13_E,
  output CELL_13_W,
  output CELL_14_E,
  output CELL_14_W,
  output CELL_15_E,
  output CELL_15_W
);

  wire and_1_out, and_2_out, and_3_out, and_4_out, and_5_out, and_6_out, and_7_out, and_8_out, and_9_out,
       and_10_out, and_11_out, and_12_out, and_13_out, and_14_out, and_15_out, and_16_out, and_17_out,
       and_18_out, and_19_out, and_20_out, and_21_out, and_22_out, and_23_out, and_24_out, and_25_out,
       and_26_out, and_27_out, and_28_out, and_29_out, and_30_out, and_31_out, and_32_out, not_1_out,
       not_2_out, not_3_out, not_4_out;

  not not_1 (not_1_out, A0);
  not not_2 (not_2_out, A1);
  not not_3 (not_3_out, A2);
  not not_4 (not_4_out, A3);
  and and_1 (and_1_out, not_1_out, not_2_out, not_3_out, not_4_out);
  and and_2 (and_2_out, A0, not_2_out, not_3_out, not_4_out);
  and and_3 (and_3_out, not_1_out, A1, not_3_out, not_4_out);
  and and_4 (and_4_out, A0, A1, not_3_out, not_4_out);
  and and_5 (and_5_out, not_1_out, not_2_out, A2, not_4_out);
  and and_6 (and_6_out, A0, not_2_out, A2, not_4_out);
  and and_7 (and_7_out, not_1_out, A1, A2, not_4_out);
  and and_8 (and_8_out, A0, A1, A2, not_4_out);
  and and_9 (and_9_out, not_1_out, not_2_out, not_3_out, A3);
  and and_10 (and_10_out, A0, not_2_out, not_3_out, A3);
  and and_11 (and_11_out, not_1_out, A1, not_3_out, A3);
  and and_12 (and_12_out, A0, A1, not_3_out, A3);
  and and_13 (and_13_out, not_1_out, not_2_out, A2, A3);
  and and_14 (and_14_out, A0, not_2_out, A2, A3);
  and and_15 (and_15_out, not_1_out, A1, A2, A3);
  and and_16 (and_16_out, A0, A1, A2, A3);
  and and_17 (and_17_out, and_1_out, OUT_CONTROL);
  Demultiplexer demultiplexer_1 (.out0(CELL_0_E), .out1(CELL_0_W), .in(and_17_out), .sel(E0W1));
  and and_18 (and_18_out, and_2_out, OUT_CONTROL);
  Demultiplexer demultiplexer_2 (.out0(CELL_1_E), .out1(CELL_1_W), .in(and_18_out), .sel(E0W1));
  and and_19 (and_19_out, and_3_out, OUT_CONTROL);
  Demultiplexer demultiplexer_3 (.out0(CELL_2_E), .out1(CELL_2_W), .in(and_19_out), .sel(E0W1));
  and and_20 (and_20_out, and_4_out, OUT_CONTROL);
  Demultiplexer demultiplexer_4 (.out0(CELL_3_E), .out1(CELL_3_W), .in(and_20_out), .sel(E0W1));
  and and_21 (and_21_out, and_5_out, OUT_CONTROL);
  Demultiplexer demultiplexer_5 (.out0(CELL_4_E), .out1(CELL_4_W), .in(and_21_out), .sel(E0W1));
  and and_22 (and_22_out, and_6_out, OUT_CONTROL);
  Demultiplexer demultiplexer_6 (.out0(CELL_5_E), .out1(CELL_5_W), .in(and_22_out), .sel(E0W1));
  and and_23 (and_23_out, and_7_out, OUT_CONTROL);
  Demultiplexer demultiplexer_7 (.out0(CELL_6_E), .out1(CELL_6_W), .in(and_23_out), .sel(E0W1));
  and and_24 (and_24_out, and_8_out, OUT_CONTROL);
  Demultiplexer demultiplexer_8 (.out0(CELL_7_E), .out1(CELL_7_W), .in(and_24_out), .sel(E0W1));
  and and_25 (and_25_out, and_9_out, OUT_CONTROL);
  Demultiplexer demultiplexer_9 (.out0(CELL_8_E), .out1(CELL_8_W), .in(and_25_out), .sel(E0W1));
  and and_26 (and_26_out, and_10_out, OUT_CONTROL);
  Demultiplexer demultiplexer_10 (.out0(CELL_9_E), .out1(CELL_9_W), .in(and_26_out), .sel(E0W1));
  and and_27 (and_27_out, and_11_out, OUT_CONTROL);
  Demultiplexer demultiplexer_11 (.out0(CELL_10_E), .out1(CELL_10_W), .in(and_27_out), .sel(E0W1));
  and and_28 (and_28_out, and_12_out, OUT_CONTROL);
  Demultiplexer demultiplexer_12 (.out0(CELL_11_E), .out1(CELL_11_W), .in(and_28_out), .sel(E0W1));
  and and_29 (and_29_out, and_13_out, OUT_CONTROL);
  Demultiplexer demultiplexer_13 (.out0(CELL_12_E), .out1(CELL_12_W), .in(and_29_out), .sel(E0W1));
  and and_30 (and_30_out, and_14_out, OUT_CONTROL);
  Demultiplexer demultiplexer_14 (.out0(CELL_13_E), .out1(CELL_13_W), .in(and_30_out), .sel(E0W1));
  and and_31 (and_31_out, and_15_out, OUT_CONTROL);
  Demultiplexer demultiplexer_15 (.out0(CELL_14_E), .out1(CELL_14_W), .in(and_31_out), .sel(E0W1));
  and and_32 (and_32_out, and_16_out, OUT_CONTROL);
  Demultiplexer demultiplexer_16 (.out0(CELL_15_E), .out1(CELL_15_W), .in(and_32_out), .sel(E0W1));
endmodule

module Down_counter (
  input  RST,
  input  Count_Enable,
  output A1,
  output A2,
  output A4,
  output A8,
  output CLK
);

  wire and_1_out, and_2_out, and_3_out, and_4_out, and_5_out, d_ff_1_q, d_ff_2_q, d_ff_3_q, d_ff_4_q,
       d_ff_5_q, d_ff_6_q, d_ff_8_qn, d_ff_9_qn, d_ff_10_qn, demultiplexer_1_out0, demultiplexer_1_out1,
       not_1_out, not_2_out, or_1_out, or_2_out, or_3_out, or_4_out, or_5_out, xor_1_out, xor_2_out,
       xor_3_out, xor_4_out, xor_5_out, xor_6_out;

  or or_1 (or_1_out, RST, d_ff_5_q);
  D_Flip_Flop d_ff_1 (.D(1'b1), .clk(demultiplexer_1_out0), .Q(d_ff_1_q), .reset(or_1_out));  // open: Qn, preset
  D_Flip_Flop d_ff_2 (.D(1'b1), .clk(demultiplexer_1_out0), .Q(d_ff_2_q), .reset(or_1_out));  // open: Qn, preset
  D_Flip_Flop d_ff_3 (.D(1'b1), .clk(demultiplexer_1_out0), .Q(d_ff_3_q), .reset(or_1_out));  // open: Qn, preset
  D_Flip_Flop d_ff_4 (.D(1'b1), .clk(demultiplexer_1_out0), .Q(d_ff_4_q), .reset(or_1_out));  // open: Qn, preset
  not not_1 (not_1_out, d_ff_5_q);
  Clock clock_1 (.out(CLK));
  and and_1 (and_1_out, not_1_out, d_ff_6_q);
  xor xor_1 (xor_1_out, and_1_out, d_ff_5_q);
  xor xor_2 (xor_2_out, d_ff_6_q, not_1_out);
  and and_2 (and_2_out, CLK, Count_Enable);
  and and_3 (and_3_out, d_ff_5_q, d_ff_8_qn, d_ff_9_qn, d_ff_10_qn);
  and and_4 (and_4_out, d_ff_5_q, d_ff_9_qn, d_ff_10_qn);
  and and_5 (and_5_out, d_ff_5_q, d_ff_10_qn);
  not not_2 (not_2_out, d_ff_10_qn);
  D_Flip_Flop d_ff_5 (.D(xor_1_out), .clk(and_2_out), .Q(d_ff_5_q), .reset(RST));  // open: Qn, preset
  D_Flip_Flop d_ff_6 (.D(xor_2_out), .clk(and_2_out), .Q(d_ff_6_q), .reset(RST));  // open: Qn, preset
  xor xor_3 (xor_3_out, A8, and_3_out);
  xor xor_4 (xor_4_out, A4, and_4_out);
  xor xor_5 (xor_5_out, A2, and_5_out);
  xor xor_6 (xor_6_out, d_ff_5_q, not_2_out);
  Demultiplexer demultiplexer_1 (
    .out0(demultiplexer_1_out0), .out1(demultiplexer_1_out1), .in(and_2_out), .sel(d_ff_5_q));
  D_Flip_Flop d_ff_7 (.D(or_2_out), .clk(demultiplexer_1_out1), .Q(A8), .reset(RST));  // open: Qn, preset
  or or_2 (or_2_out, xor_3_out, d_ff_1_q);
  D_Flip_Flop d_ff_8 (.D(or_3_out), .clk(demultiplexer_1_out1), .Q(A4), .Qn(d_ff_8_qn), .reset(RST));  // open: preset
  or or_3 (or_3_out, xor_4_out, d_ff_2_q);
  D_Flip_Flop d_ff_9 (.D(or_4_out), .clk(demultiplexer_1_out1), .Q(A2), .Qn(d_ff_9_qn), .reset(RST));  // open: preset
  or or_4 (or_4_out, xor_5_out, d_ff_3_q);
  D_Flip_Flop d_ff_10 (.D(or_5_out), .clk(demultiplexer_1_out1), .Q(A1), .Qn(d_ff_10_qn), .reset(RST));  // open: preset
  or or_5 (or_5_out, xor_6_out, d_ff_4_q);
endmodule

module thresh_control (
  input  ad_T8,
  input  ad_T4,
  input  ad_T2,
  input  ad_T1,
  input  man_T8,
  input  man_T4,
  input  man_T2,
  input  man_T1,
  input  ad_seq,
  input  load,
  output T8,
  output T4,
  output T2,
  output T1
);

  wire multiplexer_1_out, multiplexer_2_out, multiplexer_3_out, multiplexer_4_out;

  Multiplexer multiplexer_1 (.in0(man_T8), .in1(ad_T8), .out(multiplexer_1_out), .sel(ad_seq));
  Multiplexer multiplexer_2 (.in0(man_T4), .in1(ad_T4), .out(multiplexer_2_out), .sel(ad_seq));
  Multiplexer multiplexer_3 (.in0(man_T2), .in1(ad_T2), .out(multiplexer_3_out), .sel(ad_seq));
  Multiplexer multiplexer_4 (.in0(man_T1), .in1(ad_T1), .out(multiplexer_4_out), .sel(ad_seq));
  thresh_reg thresh_reg_1 (
    .I8(multiplexer_1_out), .I4(multiplexer_2_out), .I2(multiplexer_3_out), .I1(multiplexer_4_out),
    .load(load), .T8(T8), .T4(T4), .T2(T2), .T1(T1));
endmodule

module thresh_reg (
  input  I8,
  input  I4,
  input  I2,
  input  I1,
  input  load,
  output T8,
  output T4,
  output T2,
  output T1
);

  D_Flip_Flop d_ff_1 (.D(I8), .clk(load), .Q(T8));  // open: Qn, preset, reset
  D_Flip_Flop d_ff_2 (.D(I4), .clk(load), .Q(T4));  // open: Qn, preset, reset
  D_Flip_Flop d_ff_3 (.D(I2), .clk(load), .Q(T2));  // open: Qn, preset, reset
  D_Flip_Flop d_ff_4 (.D(I1), .clk(load), .Q(T1));  // open: Qn, preset, reset
endmodule

module synchronizer (
  input  sync_en,
  input  rst,
  output clk_sync
);

  wire and_1_out, and_2_out, and_3_out, and_4_out, clock_1_out, d_ff_1_q, d_ff_2_q, not_1_out, not_2_out,
       xor_1_out, xor_2_out;

  and and_1 (and_1_out, d_ff_1_q, d_ff_2_q);
  not not_1 (not_1_out, and_1_out);
  and and_2 (and_2_out, not_1_out, d_ff_2_q);
  and and_3 (and_3_out, d_ff_1_q, d_ff_2_q);
  not not_2 (not_2_out, and_3_out);
  Clock clock_1 (.out(clock_1_out));
  D_Flip_Flop d_ff_1 (.D(xor_1_out), .clk(and_4_out), .Q(d_ff_1_q), .reset(rst));  // open: Qn, preset
  xor xor_1 (xor_1_out, d_ff_1_q, and_2_out);
  D_Flip_Flop d_ff_2 (.D(xor_2_out), .clk(and_4_out), .Q(d_ff_2_q), .reset(rst));  // open: Qn, preset
  xor xor_2 (xor_2_out, d_ff_2_q, not_2_out);
  and and_4 (and_4_out, clock_1_out, sync_en);
  and and_5 (clk_sync, d_ff_1_q, d_ff_2_q);
endmodule

module cycle_synchronizer (
  input  ad_seq_in,
  input  clk_in,
  input  rst,
  input  dc_A1,
  input  dc_A2,
  input  dc_A4,
  input  dc_A8,
  output chip_en_in,
  output load,
  output ad_seq
);

  wire and_1_out, d_ff_2_q, synchronizer_1_clk_sync;

  D_Flip_Flop d_ff_1 (.D(1'b1), .clk(and_1_out), .Q(chip_en_in), .reset(rst));  // open: Qn, preset
  and and_1 (and_1_out, dc_A8, dc_A4, dc_A2, dc_A1);
  D_Flip_Flop d_ff_2 (.D(1'b1), .clk(synchronizer_1_clk_sync), .Q(d_ff_2_q), .reset(rst));  // open: Qn, preset
  and and_2 (ad_seq, chip_en_in, ad_seq_in);
  synchronizer synchronizer_1 (.sync_en(ad_seq_in), .rst(rst), .clk_sync(synchronizer_1_clk_sync));
  and and_3 (load, clk_in, ad_seq_in, d_ff_2_q);
endmodule

module control_loop (
  input  MEM_RST,
  input  MEM_P_EN,
  input  D1,
  input  D2,
  input  D4,
  input  D8,
  input  ERROR_IN,
  input  E0W1,
  input  M_LRST,
  input  T8,
  input  T4,
  input  T2,
  input  T1,
  input  M_TL,
  input  rearm,
  output CLK,
  output A1V,
  output A2V,
  output A4V,
  output A8V,
  output TO8,
  output TO4,
  output TO2,
  output TO1,
  output ad_seq
);

  wire cycle_synchronizer_1_chip_en_in, cycle_synchronizer_1_load, d_ff_1_q, or_1_out, or_2_out,
       thresh_memory_1_o1, thresh_memory_1_o2, thresh_memory_1_o4, thresh_memory_1_o8;

  D_Flip_Flop d_ff_1 (.D(1'b1), .clk(ERROR_IN), .Q(d_ff_1_q), .reset(or_1_out));  // open: Qn, preset
  or or_1 (or_1_out, rearm, M_LRST);
  Down_counter down_counter_1 (
    .RST(or_1_out), .Count_Enable(d_ff_1_q), .A1(A1V), .A2(A2V), .A4(A4V), .A8(A8V), .CLK(CLK));
  thresh_memory thresh_memory_1 (
    .RESET(MEM_RST), .Mem_Prog_EN(MEM_P_EN), .D1(D1), .D2(D2), .D4(D4), .D8(D8), .A1(A1V), .A2(A2V),
    .A4(A4V), .A8(A8V), .CHIP_EN(cycle_synchronizer_1_chip_en_in), .E0W1(E0W1), .O1(thresh_memory_1_o1),
    .O2(thresh_memory_1_o2), .O4(thresh_memory_1_o4), .O8(thresh_memory_1_o8));
  cycle_synchronizer cycle_synchronizer_1 (
    .ad_seq_in(d_ff_1_q), .clk_in(CLK), .rst(or_1_out), .dc_A1(A1V), .dc_A2(A2V), .dc_A4(A4V), .dc_A8(A8V),
    .chip_en_in(cycle_synchronizer_1_chip_en_in), .load(cycle_synchronizer_1_load), .ad_seq(ad_seq));
  or or_2 (or_2_out, cycle_synchronizer_1_load, M_TL);
  thresh_control thresh_control_1 (
    .ad_T8(thresh_memory_1_o8), .ad_T4(thresh_memory_1_o4), .ad_T2(thresh_memory_1_o2),
    .ad_T1(thresh_memory_1_o1), .man_T8(T8), .man_T4(T4), .man_T2(T2), .man_T1(T1), .ad_seq(ad_seq),
    .load(or_2_out), .T8(TO8), .T4(TO4), .T2(TO2), .T1(TO1));
endmodule
